# Fritzing sketch System_Fritzing_Diagram (saved by Fritzing 0.8.5b)
breadboards: 1

parts:
  M1 = DC Motor  # not connected
  J2 = Infrared Proximity Sensor  # not connected
  Raspberry_Pi_1 = Raspberry Pi 3
  J3 = Basic Servo
  VCC1 = 4 x AAA Battery Mount  # not connected
  Part1 = Tri-Axis Gyro Breakout - L3G4200D  # not connected
  IC1 = L293D [package=THT]  # not connected

nets:
  GND: Raspberry_Pi_1.GND, J3.gnd
  N1: Raspberry_Pi_1.GIPO12, J3.pulse
  5V: Raspberry_Pi_1.5V, J3.vcc
